// Logisim project AdderSubCircuit.circ as structural Verilog: 1 circuit, main circuit main
module main (
  input  B4,
  input  A4,
  input  B3,
  input  A3,
  input  B2,
  input  A2,
  input  B1,
  input  A1
);

  wire n74283_1_pin1, n74283_1_pin4, n74283_1_pin8, n74283_1_pin10, n74283_1_pin13, n74283_1_pin16;

  _74283 #(.ShowInternalStructure("true"), .VccGndPorts("true")) u_74283_1 (
    .pin1(n74283_1_pin1), .pin2(B2), .pin3(A2), .pin4(n74283_1_pin4), .pin5(A1), .pin6(B1),
    .pin8(n74283_1_pin8), .pin16(n74283_1_pin16), .pin15(B3), .pin14(A3), .pin13(n74283_1_pin13), .pin12(A4),
    .pin11(B4), .pin10(n74283_1_pin10));  // open: pin7, pin9
  LED O3 (.in(n74283_1_pin10));
  LED O2 (.in(n74283_1_pin13));
  LED O1 (.in(n74283_1_pin1));
  LED O0 (.in(n74283_1_pin4));
  // also tied to GND on the sheet: n74283_1_pin8
  // also tied to VCC on the sheet: n74283_1_pin16
endmodule
